# Fritzing sketch OLED_128x64_i2c (saved by Fritzing 0.7.5b)
breadboards: 1

parts:
  WeMos_D1_Mini1 = WeMos D1 Mini
  OLED_I2C1 = OLED 128x64 I2C Monochrome Display
  R1 = Resistor [tolerance=±5% resistance=10k part_number=10kΩ package=THT]
  R2 = Resistor [tolerance=±5% resistance=10k package=THT]

nets:
  3V3: WeMos_D1_Mini1.3V3, OLED_I2C1.VDD, R1.Pin_0, R2.Pin_1
  N1: WeMos_D1_Mini1.D1, OLED_I2C1.SDA, R1.Pin_1
  N2: WeMos_D1_Mini1.D3, OLED_I2C1.SCK, R2.Pin_0
  N3: WeMos_D1_Mini1.G, OLED_I2C1.GND
